// Logisim project SingleCycle_CPU.circ as structural Verilog
module Reg_File (
  input  [1:0] Read_Reg_1,
  input  [1:0] Read_Reg_2,
  input  [31:0] Write_Data,
  input  [1:0] Write_Reg,
  input  RegWrite,
  input  CLK,
  input  Reset,
  output [31:0] Read_Data_1,
  output [31:0] Read_Data_2
);

  wire decoder_1_out0, decoder_1_out1, decoder_1_out2, decoder_1_out3;
  wire [31:0] R0, R1, R2, R3;

  Decoder #(.select(2)) decoder_1 (
    .out0(decoder_1_out0), .out1(decoder_1_out1), .out2(decoder_1_out2), .out3(decoder_1_out3),
    .sel(Write_Reg), .en(RegWrite));
  Register #(.width(32)) u_R0 (.D({32{1'b0}}), .en(decoder_1_out0), .clk(CLK), .Q(R0), .clr(Reset));
  Register #(.width(32)) u_R1 (.D(Write_Data), .en(decoder_1_out1), .clk(CLK), .Q(R1), .clr(Reset));
  Register #(.width(32)) u_R2 (.D(Write_Data), .en(decoder_1_out2), .clk(CLK), .Q(R2), .clr(Reset));
  Register #(.width(32)) u_R3 (.D(Write_Data), .en(decoder_1_out3), .clk(CLK), .Q(R3), .clr(Reset));
  Multiplexer #(.select(2), .width(32), .enable("false")) multiplexer_1 (
    .in0(R0), .in1(R1), .in2(R2), .in3(R3), .out(Read_Data_1), .sel(Read_Reg_1));
  Multiplexer #(.select(2), .width(32), .enable("false")) multiplexer_2 (
    .in0(R0), .in1(R1), .in2(R2), .in3(R3), .out(Read_Data_2), .sel(Read_Reg_2));

  // Other names for the same wires on the sheet: ReadR1[1:0] = Read_Reg_1; ReadR2[1:0] = Read_Reg_2
endmodule
